# Fritzing sketch PicoConnections (saved by Fritzing 0.9.6b)
breadboards: 1

parts:
  Mod1 = Raspberry Pi Pico
  LCD_12864-06D1 = 128 x 64 Graphic LCD [part_number="CMG 12864-06D"]
  R1 = Resistor [tolerance=±5% power=0.25 resistance=220 package=THT]

nets:
  N1: Mod1.pin_3, Mod1.pin_8, Mod1.pin_13, Mod1.pin_18, Mod1.pin_23, Mod1.pin_28, Mod1.pin_33, Mod1.pin_38, LCD_12864-06D1.7_GND, LCD_12864-06D1.9_LEDK
  N2: Mod1.pin_21, LCD_12864-06D1.12_IC_SDO
  N3: Mod1.pin_22, LCD_12864-06D1.1_/CS
  N4: Mod1.pin_24, LCD_12864-06D1.4_SCK, LCD_12864-06D1.10_IC_SCK
  N5: Mod1.pin_25, LCD_12864-06D1.5_SI, LCD_12864-06D1.13_IC_SDI
  N6: Mod1.pin_26, LCD_12864-06D1.2_RES
  N7: Mod1.pin_27, LCD_12864-06D1.3_RS
  N8: Mod1.pin_29, LCD_12864-06D1.11_IC_CS
  N9: Mod1.pin_36, LCD_12864-06D1.6_VDD, R1.Pin_0
  N10: LCD_12864-06D1.8_LEDA, R1.Pin_1

custom parts:
  Raspberry Pi Pico: Raspberry Pi Pico. Based around the RP2040 microcontroller the Pico is a low cost microcontroller device bringing Raspberry Pi quality, cost, and easy of use to the microcontroller space. Jan 2021, Split part in to two versions: tht (this one) and SMD. This one will drill holes for a .1 in header in pcb to allow plugging in the module as well as providing pads to solder the module to the top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
  128 x 64 Graphic LCD: Graphic LCD display 128x64 resolution ST7565R controller, 16S1Y / ER3805-1 SPI font ROM
